// Logisim project additionneur.circ as structural Verilog: 7 circuits, main circuit main
module main (
  input  in_1,
  input  in_2,
  input  in_3,
  input  in_4,
  input  in_5,
  input  in_6,
  input  in_7,
  input  in_8,
  input  in_9
);

  wire add_sous_1_out_10, add_sous_1_out_11, add_sous_1_out_12, add_sous_1_out_13, add_sous_1_out_14,
       transform_1_out_5, transform_2_out_5, transform_3_out_5;
  wire [3:0] transform_1_out_6, transform_2_out_6, transform_3_out_6;

  transform transform_1 (
    .out_5(transform_1_out_5), .out_6(transform_1_out_6), .in_1(in_7), .in_2(in_5), .in_3(in_3), .in_4(in_1));
  Hex_Digit_Display hex_digit_display_1 (.value(transform_1_out_6), .dp(transform_1_out_5));
  transform transform_2 (
    .out_5(transform_2_out_5), .out_6(transform_2_out_6), .in_1(add_sous_1_out_11), .in_2(add_sous_1_out_12),
    .in_3(add_sous_1_out_13), .in_4(add_sous_1_out_14));
  Add_Sous add_sous_1 (
    .out_10(add_sous_1_out_10), .in_9(in_9), .in_5(in_7), .in_6(in_5), .in_7(in_3), .in_8(in_1), .in_1(in_8),
    .in_2(in_6), .in_3(in_4), .in_4(in_2), .out_11(add_sous_1_out_11), .out_12(add_sous_1_out_12),
    .out_13(add_sous_1_out_13), .out_14(add_sous_1_out_14));
  Hex_Digit_Display hex_digit_display_2 (.value(transform_2_out_6), .dp(transform_2_out_5));
  transform transform_3 (
    .out_5(transform_3_out_5), .out_6(transform_3_out_6), .in_1(in_8), .in_2(in_6), .in_3(in_4), .in_4(in_2));
  Hex_Digit_Display hex_digit_display_3 (.value(transform_3_out_6), .dp(transform_3_out_5));
endmodule

module Sum2 (
  input  a,
  input  b,
  output s,
  output r
);

  xor xor_1 (s, b, a);
  and and_1 (r, b, a);
endmodule

module Sum3 (
  input  a,
  input  b,
  input  in_3,
  output out_4,
  output out_5
);

  wire sum2_1_r, sum2_2_r, sum2_2_s;

  xor xor_1 (out_4, sum2_2_r, sum2_1_r);
  Sum2 sum2_1 (.s(out_5), .r(sum2_1_r), .a(a), .b(sum2_2_s));
  Sum2 sum2_2 (.s(sum2_2_s), .r(sum2_2_r), .a(b), .b(in_3));
endmodule

module Add_4bit (
  input  in_1,
  input  in_2,
  input  in_3,
  input  in_4,
  input  in_5,
  input  in_6,
  input  in_7,
  input  in_8,
  input  in_9,
  output out_10,
  output out_11,
  output out_12,
  output out_13,
  output out_14
);

  wire sum3_2_out_4, sum3_3_out_4, sum3_4_out_4;

  Sum3 sum3_1 (.in_3(sum3_2_out_4), .a(in_1), .b(in_5), .out_5(out_11), .out_4(out_10));
  Sum3 sum3_2 (.in_3(sum3_3_out_4), .a(in_2), .b(in_6), .out_5(out_12), .out_4(sum3_2_out_4));
  Sum3 sum3_3 (.in_3(sum3_4_out_4), .a(in_3), .b(in_7), .out_5(out_13), .out_4(sum3_3_out_4));
  Sum3 sum3_4 (.in_3(in_9), .a(in_4), .b(in_8), .out_5(out_14), .out_4(sum3_4_out_4));
endmodule

module Sous_4bit (
  input  in_1,
  input  in_2,
  input  in_3,
  input  in_4,
  input  in_5,
  input  in_6,
  input  in_7,
  input  in_8,
  output out_9,
  output out_10,
  output out_11,
  output out_12,
  output out_13
);

  wire not_1_out, not_2_out, not_3_out, not_4_out;

  not not_1 (not_1_out, in_2);
  not not_2 (not_2_out, in_3);
  not not_3 (not_3_out, in_4);
  not not_4 (not_4_out, in_1);
  Add_4bit add_4bit_1 (
    .out_10(out_9), .in_9(1'b1), .in_1(in_5), .in_5(not_4_out), .in_2(in_6), .in_6(not_1_out), .in_3(in_7),
    .in_7(not_2_out), .in_4(in_8), .in_8(not_3_out), .out_11(out_10), .out_12(out_11), .out_13(out_12),
    .out_14(out_13));
endmodule

module Add_Sous (
  input  in_1,
  input  in_2,
  input  in_3,
  input  in_4,
  input  in_5,
  input  in_6,
  input  in_7,
  input  in_8,
  input  in_9,
  output out_10,
  output out_11,
  output out_12,
  output out_13,
  output out_14
);

  wire xor_1_out, xor_2_out, xor_3_out, xor_4_out;

  xor xor_1 (xor_1_out, in_1, in_9);
  Add_4bit add_4bit_1 (
    .out_10(out_10), .in_9(in_9), .in_1(in_5), .in_5(xor_1_out), .in_2(in_6), .in_6(xor_2_out), .in_3(in_7),
    .in_7(xor_3_out), .in_4(in_8), .in_8(xor_4_out), .out_11(out_11), .out_12(out_12), .out_13(out_13),
    .out_14(out_14));
  xor xor_2 (xor_2_out, in_2, in_9);
  xor xor_3 (xor_3_out, in_3, in_9);
  xor xor_4 (xor_4_out, in_4, in_9);
endmodule

module transform (
  input  in_1,
  input  in_2,
  input  in_3,
  input  in_4,
  output out_5,
  output [3:0] out_6
);

  Add_Sous add_sous_1 (
    .in_9(in_1), .in_5(1'b0), .in_6(1'b0), .in_7(1'b0), .in_8(1'b0), .in_1(in_1), .in_2(in_2), .in_3(in_3),
    .in_4(in_4), .out_11(out_6[3]), .out_12(out_6[2]), .out_13(out_6[1]), .out_14(out_6[0]));  // open: out_10

  assign out_5 = in_1;
endmodule
