// Logisim project circuits.circ as structural Verilog: 4 circuits, main circuit main
module main (
  input  in_1,
  input  in_2,
  input  in_3,
  input  in_4,
  input  in_5,
  input  in_6,
  input  in_7,
  input  Piece,
  input  Menthe,
  input  Cassis,
  input  Eau,
  output out_12,
  output out_13,
  output Eau_2,
  output Cassis_2,
  output Menthe_2,
  output Rendu
);

  wire button_1_out, exo_3_1_a, exo_3_1_c, exo_3_1_r, exo_3_1_v;

  LED led_1 (.in(exo_3_1_c));
  LED led_2 (.in(exo_3_1_v));
  LED led_3 (.in(exo_3_1_a));
  Button button_1 (.out(button_1_out));
  Exo_3 exo_3_1 (
    .V(exo_3_1_v), .C(exo_3_1_c), .R(exo_3_1_r), .A(exo_3_1_a), .CV(in_4), .CC(in_5), .CR(in_6), .CA(in_7));
  LED led_4 (.in(exo_3_1_r));
  Exo_2 exo_2_1 (.A(in_1), .B(in_2), .C(in_3), .R(out_12), .S(out_13));
  Exo_4 exo_4_1 (
    .EAU_2(Eau_2), .CASSIS_2(Cassis_2), .MENTHE_2(Menthe_2), .RENDU(Rendu), .Eau(Eau), .Cassis(Cassis),
    .Menthe(Menthe), .Piece(Piece), .in_5(button_1_out));
  LED led_5 (.in(exo_3_1_a));
  LED led_6 (.in(exo_3_1_c));
  LED led_7 (.in(exo_3_1_r));
  LED led_8 (.in(exo_3_1_v));

  // Notes on the sheet:
  //   Validation
endmodule

module Exo_2 (
  input  A,
  input  B,
  input  C,
  output R,
  output S
);

  wire and_1_out, and_2_out, and_3_out;

  or or_1 (R, A, C, B);
  and and_1 (and_1_out, A, B);
  and and_2 (and_2_out, A, C);
  and and_3 (and_3_out, B, C, C);
  or or_2 (S, and_1_out, and_2_out, and_3_out);
endmodule

module Exo_3 (
  input  CV,
  input  CC,
  input  CR,
  input  CA,
  output V,
  output C,
  output R,
  output A
);

  wire not_1_out, not_2_out;

  not not_1 (not_1_out, CC);
  not not_2 (not_2_out, CA);
  or or_1 (V, CV, CC, CR, CA);
  and and_1 (R, not_1_out, CR, not_2_out);
  and and_2 (A, not_1_out, CA);

  assign C = CC;
endmodule

module Exo_4 (
  input  Eau,
  input  Cassis,
  input  Menthe,
  input  Piece,
  input  in_5,
  output EAU_2,
  output CASSIS_2,
  output MENTHE_2,
  output RENDU
);

  wire and_1_out, and_2_out, and_3_out, and_6_out, and_7_out, and_8_out, not_1_out, not_2_out, not_3_out;

  not not_1 (not_1_out, Eau);
  not not_2 (not_2_out, Cassis);
  not not_3 (not_3_out, Menthe);
  and and_1 (and_1_out, in_5, Eau, not_3_out, Piece);
  and and_2 (and_2_out, in_5, Eau, not_2_out, not_3_out);
  and and_3 (and_3_out, in_5, Eau, not_2_out, Piece);
  and and_4 (CASSIS_2, Eau, Cassis, not_3_out, Piece, in_5);
  and and_5 (MENTHE_2, Eau, not_2_out, Menthe, Piece, in_5);
  and and_6 (and_6_out, not_1_out, Piece, in_5);
  and and_7 (and_7_out, Cassis, Menthe, Piece, in_5);
  and and_8 (and_8_out, not_2_out, not_3_out, Piece, in_5);
  or or_1 (EAU_2, and_1_out, and_2_out, and_3_out);
  or or_2 (RENDU, and_6_out, and_7_out, and_8_out);
endmodule
