// Logisim project Tp_2.circ as structural Verilog: 1 circuit, main circuit main
module main (
  input  E3,
  input  E2,
  input  E1,
  input  E0,
  output out_5,
  output out_6,
  output out_7,
  output out_8,
  output out_9,
  output out_10,
  output out_11,
  output out_12,
  output out_13,
  output out_14
);

  wire not_1_out, not_2_out, not_3_out, not_4_out;

  not not_1 (not_1_out, E3);
  not not_2 (not_2_out, E1);
  not not_3 (not_3_out, E2);
  not not_4 (not_4_out, E0);
  and and_1 (out_5, E0, E1, not_3_out, not_1_out);
  and and_2 (out_6, not_4_out, not_2_out, E2, not_1_out);
  and and_3 (out_7, E0, not_2_out, E2, not_1_out);
  and and_4 (out_8, not_4_out, E1, E2, not_1_out);
  and and_5 (out_9, E0, E1, E2, not_1_out);
  and and_6 (out_10, not_4_out, not_2_out, not_3_out, E3);
  and and_7 (out_11, E0, not_2_out, not_3_out, E3);
  and and_8 (out_12, not_4_out, E1, not_3_out, E3);
  and and_9 (out_13, E0, E1, not_3_out, E3);
  and and_10 (out_14, not_4_out, not_2_out, E2, E3);
endmodule
