// Logisim project afficheur.circ as structural Verilog: 2 circuits, main circuit main
module main (
);

  wire decodeur_1_a, decodeur_1_b, decodeur_1_c, decodeur_1_d, decodeur_1_e, decodeur_1_f, decodeur_1_g,
       E0_out, E1_out, E2_out, E3_out;

  Clock #(.highDuration(8), .lowDuration(8)) E3 (.out(E3_out));
  Clock #(.highDuration(4), .lowDuration(4)) E2 (.out(E2_out));
  Clock E0 (.out(E0_out));
  Clock #(.highDuration(2), .lowDuration(2)) E1 (.out(E1_out));
  decodeur decodeur_1 (
    .a(decodeur_1_a), .b(decodeur_1_b), .c(decodeur_1_c), .d(decodeur_1_d), .e(decodeur_1_e),
    .f(decodeur_1_f), .g(decodeur_1_g), .E3(E3_out), .E2(E2_out), .E1(E1_out), .E0(E0_out));
  _7_Segment_Display u_7_segment_display_1 (
    .g(decodeur_1_g), .f(decodeur_1_f), .a(decodeur_1_a), .b(decodeur_1_b), .e(decodeur_1_e),
    .d(decodeur_1_d), .c(decodeur_1_c));  // open: dp
endmodule

module decodeur (
  input  E3,
  input  E2,
  input  E1,
  input  E0,
  output a,
  output b,
  output c,
  output d,
  output e,
  output f,
  output g
);

  wire and_1_out, and_2_out, and_3_out, and_4_out, and_5_out, and_6_out, and_7_out, and_8_out, and_9_out,
       and_10_out, and_11_out, and_12_out, and_13_out, and_14_out, not_1_out, not_2_out, not_3_out, not_4_out;

  not not_1 (not_1_out, E3);
  not not_2 (not_2_out, E2);
  not not_3 (not_3_out, E1);
  not not_4 (not_4_out, E0);
  and and_1 (and_1_out, not_3_out, E0);
  and and_2 (and_2_out, E1, not_4_out);
  and and_3 (and_3_out, E0, not_2_out);
  and and_4 (and_4_out, not_3_out, E3);
  and and_5 (and_5_out, not_3_out, E0);
  and and_6 (and_6_out, not_4_out, E1, not_1_out);
  and and_7 (and_7_out, E0, not_3_out);
  and and_8 (and_8_out, E0, not_2_out);
  and and_9 (and_9_out, E0, E1);
  and and_10 (and_10_out, not_3_out, E3);
  and and_11 (and_11_out, E3, not_3_out);
  and and_12 (and_12_out, E3, E0);
  and and_13 (and_13_out, E0, E2);
  and and_14 (and_14_out, E1, E2);
  or or_1 (e, and_7_out, and_8_out);
  or or_2 (a, and_1_out, and_2_out, not_2_out, E3);
  or or_3 (b, E1, E2);
  or or_4 (c, E3, E1, not_4_out);
  or or_5 (d, and_3_out, and_4_out, and_5_out, and_6_out);
  or or_6 (f, and_9_out, and_10_out);
  or or_7 (g, and_11_out, and_12_out, and_13_out, and_14_out);
endmodule
