// Logisim project Tp_bascule.circ as structural Verilog: 3 circuits, main circuit main
module main (
  output out_1,
  output out_2,
  output out_3,
  output out_4,
  output out_5,
  output out_6,
  output out_7,
  output out_8,
  output out_9,
  output out_10,
  output out_11,
  output out_12
);

  wire button_1_out, clock_1_out, xor_1_out;

  Button button_1 (.out(button_1_out));
  Clock clock_1 (.out(clock_1_out));
  xor xor_1 (xor_1_out, button_1_out, out_1);
  Exo_2 exo_2_1 (.in_2(clock_1_out), .in_1(out_4), .out_3(out_3), .out_4(out_2), .out_5(out_1));
  Exo_2 exo_2_2 (.in_2(clock_1_out), .in_1(out_7), .out_3(out_6), .out_4(out_5), .out_5(out_4));
  Exo_2 exo_2_3 (.in_2(clock_1_out), .in_1(out_10), .out_3(out_9), .out_4(out_8), .out_5(out_7));
  Exo_2 exo_2_4 (.in_2(clock_1_out), .in_1(xor_1_out), .out_3(out_12), .out_4(out_11), .out_5(out_10));
endmodule

module compteur (
  input  C,
  input  H,
  output S2,
  output S1,
  output S0
);

  wire and_1_out, and_2_out, not_1_out, not_2_out, not_4_out, or_1_out, or_2_out;

  not not_1 (not_1_out, C);
  not not_2 (not_2_out, S2);
  // NOT_Gate not_3 has open pins: in=S0, out=open
  not not_4 (not_4_out, S1);
  and and_1 (and_1_out, not_4_out, not_2_out);
  and and_2 (and_2_out, S1, S0);
  J_K_Flip_Flop j_k_ff_1 (.J(or_1_out), .clk(H), .K(not_4_out), .Q(S0));  // open: Qn, preset, en, reset
  or or_1 (or_1_out, and_1_out, C);
  J_K_Flip_Flop j_k_ff_2 (.J(S0), .clk(H), .K(not_2_out), .Q(S1));  // open: Qn, preset, en, reset
  J_K_Flip_Flop j_k_ff_3 (.J(S1), .clk(H), .K(or_2_out), .Q(S2));  // open: Qn, preset, en, reset
  or or_2 (or_2_out, not_1_out, and_2_out);
endmodule

module Exo_2 (
  input  in_1,
  input  in_2,
  output out_3,
  output out_4,
  output out_5
);

  wire j_k_ff_1_qn, j_k_ff_2_qn, not_1_out;

  not not_1 (not_1_out, in_1);
  J_K_Flip_Flop j_k_ff_1 (.J(in_1), .clk(in_2), .K(not_1_out), .Q(out_3), .Qn(j_k_ff_1_qn));  // open: preset, en, reset
  J_K_Flip_Flop j_k_ff_2 (
    .J(out_3), .clk(in_2), .K(j_k_ff_1_qn), .Q(out_4), .Qn(j_k_ff_2_qn));  // open: preset, en, reset
  J_K_Flip_Flop j_k_ff_3 (.J(out_4), .clk(in_2), .K(j_k_ff_2_qn), .Q(out_5));  // open: Qn, preset, en, reset
endmodule
