// Logisim project PIso1-ROM-Vide.circ as structural Verilog: 21 circuits, main circuit Processeur
module Processeur (
  input  in_1
);

  wire Clock, Comp, CS_DEC_ALU, CSMem, e_PC, e_RA, e_RAD_b, e_RAD_h, e_RAP_b, e_RAP_h, e_RB, e_RC, e_RE,
       e_RI, Inc_PC, l_PC, l_RA_A, l_RA_B, l_RAD, l_RAP, l_RB, l_RC, l_RE, l_RI_b, l_RI_h, R_nw, Raz_PC;
  wire [3:0] aff_2_1_out_3, aff_2_1_out_4, aff_2_2_out_3, aff_2_2_out_4, aff_2_3_out_3, aff_2_3_out_4,
       aff_2_4_out_3, aff_2_4_out_4, aff_2_5_out_3, aff_2_5_out_4, aff_2_6_out_3, aff_2_6_out_4,
       aff_4_1_out_3, aff_4_1_out_4, aff_4_1_out_5, aff_4_1_out_6, aff_4_2_out_3, aff_4_2_out_4,
       aff_4_2_out_5, aff_4_2_out_6, aff_4_3_out_3, aff_4_3_out_4, aff_4_3_out_5, aff_4_3_out_6,
       aff_4_4_out_3, aff_4_4_out_4, aff_4_4_out_5, aff_4_4_out_6, Code_Inst, ri_1_ob;
  wire [7:0] alu_1_r, alu_1_x_x_i_o_c_p_s_z, ra_1_oa, ra_1_ob, ra_1_out_5, rb_1_o, rb_1_out_4, rc_1_out_4,
       ri_1_out_5, ucom_1_out_5, ucom_1_out_7;
  wire [15:0] pc_1_out_7, rad_1_out_5, rad_1_out_6, rap_1_out_5, rap_1_out_6;

  Clock clock_1 (.out(Clock));
  Hex_Digit_Display hex_digit_display_1 (.value(aff_4_1_out_3));  // open: dp
  Aff_4 aff_4_1 (
    .out_3(aff_4_1_out_3), .out_4(aff_4_1_out_4), .out_5(aff_4_1_out_5), .out_6(aff_4_1_out_6),
    .in_2(rad_1_out_5));  // open: in_1
  Hex_Digit_Display hex_digit_display_2 (.value(aff_4_1_out_5));  // open: dp
  Hex_Digit_Display hex_digit_display_3 (.value(aff_4_1_out_4));  // open: dp
  Hex_Digit_Display hex_digit_display_4 (.value(aff_4_1_out_6));  // open: dp
  Aff_2 aff_2_1 (.in_1(ucom_1_out_5), .out_3(aff_2_1_out_3), .out_4(aff_2_1_out_4));  // open: in_2
  Hex_Digit_Display hex_digit_display_5 (.value(aff_2_1_out_3));  // open: dp
  Hex_Digit_Display hex_digit_display_6 (.value(aff_2_1_out_4));  // open: dp
  RAD rad_1 (.in_3(e_RAD_h), .in_2(e_RAD_b), .in_4(l_RAD), .in_1(ra_1_oa), .out_6(rad_1_out_6), .out_5(rad_1_out_5));
  Hex_Digit_Display hex_digit_display_7 (.value(aff_4_2_out_3));  // open: dp
  Hex_Digit_Display hex_digit_display_8 (.value(aff_4_2_out_4));  // open: dp
  Hex_Digit_Display hex_digit_display_9 (.value(Code_Inst));  // open: dp
  LED led_1 (.in(Comp));
  UCom ucom_1 (
    .in_1(Code_Inst), .in_2(Comp), .in_4(in_1), .in_3(Clock),
    .out_6({CSMem, R_nw, e_RE, l_RE, e_RC, l_RC, l_RB, e_RB, l_RA_A, e_RA, l_RA_B, l_RI_b, e_RI, l_RI_h, l_PC, e_PC, l_RAP, e_RAP_b, e_RAP_h, Raz_PC, Inc_PC, l_RAD, e_RAD_b, e_RAD_h}),
    .CS_DEC_ALU(CS_DEC_ALU), .out_7(ucom_1_out_7), .out_5(ucom_1_out_5));
  Aff_4 aff_4_2 (
    .out_3(aff_4_2_out_3), .out_4(aff_4_2_out_4), .out_5(aff_4_2_out_5), .out_6(aff_4_2_out_6),
    .in_2(rap_1_out_5));  // open: in_1
  Hex_Digit_Display hex_digit_display_10 (.value(aff_4_2_out_5));  // open: dp
  Hex_Digit_Display hex_digit_display_11 (.value(aff_4_2_out_6));  // open: dp
  Hex_Digit_Display hex_digit_display_12 (.value(aff_4_3_out_3));  // open: dp
  RAP rap_1 (.in_3(e_RAP_h), .in_2(e_RAP_b), .in_4(l_RAP), .in_1(ra_1_oa), .out_6(rap_1_out_6), .out_5(rap_1_out_5));
  PC pc_1 (
    .e(e_PC), .INC(Inc_PC), .RAZ(Raz_PC), .l(l_PC), .O(rad_1_out_6), .I(rap_1_out_6), .out_7(pc_1_out_7),
    .Clock(Clock));
  Aff_4 aff_4_3 (
    .in_1(pc_1_out_7), .out_3(aff_4_3_out_3), .out_4(aff_4_3_out_4), .out_5(aff_4_3_out_5),
    .out_6(aff_4_3_out_6));  // open: in_2
  Hex_Digit_Display hex_digit_display_13 (.value(aff_4_3_out_4));  // open: dp
  Hex_Digit_Display hex_digit_display_14 (.value(aff_4_3_out_5));  // open: dp
  LED E_C_ROM (.in(ucom_1_out_7[7]));
  LED I_C_ROM (.in(ucom_1_out_7[6]));
  LED R_C_ROM (.in(ucom_1_out_7[5]));
  LED CS_MUX_DEC (.in(ucom_1_out_7[4]));
  LED CS_MUX_ETAT (.in(ucom_1_out_7[3]));
  LED u_CS_DEC_ALU (.in(ucom_1_out_7[2]));
  Hex_Digit_Display hex_digit_display_15 (.value(aff_4_3_out_6));  // open: dp
  Aff_2 aff_2_2 (.in_1(ri_1_out_5), .out_3(aff_2_2_out_3), .out_4(aff_2_2_out_4));  // open: in_2
  Hex_Digit_Display hex_digit_display_16 (.value(aff_2_2_out_3));  // open: dp
  Hex_Digit_Display hex_digit_display_17 (.value(aff_2_2_out_4));  // open: dp
  RI ri_1 (.eRI(e_RI), .lRIh(l_RI_h), .lRIb(l_RI_b), .I(ra_1_oa), .oH(Code_Inst), .oB(ri_1_ob), .out_5(ri_1_out_5));
  Aff_2 aff_2_3 (.in_1(ra_1_out_5), .out_3(aff_2_3_out_3), .out_4(aff_2_3_out_4));  // open: in_2
  Hex_Digit_Display hex_digit_display_18 (.value(aff_2_3_out_4));  // open: dp
  Hex_Digit_Display hex_digit_display_19 (.value(aff_2_3_out_3));  // open: dp
  RA ra_1 (.e(e_RA), .lA(l_RA_B), .lB(l_RA_A), .I(ra_1_oa), .oA(ra_1_oa), .oB(ra_1_ob), .out_5(ra_1_out_5));
  Aff_2 aff_2_4 (.in_1(rb_1_out_4), .out_3(aff_2_4_out_3), .out_4(aff_2_4_out_4));  // open: in_2
  Hex_Digit_Display hex_digit_display_20 (.value(aff_2_4_out_4));  // open: dp
  Hex_Digit_Display hex_digit_display_21 (.value(aff_2_4_out_3));  // open: dp
  RB rb_1 (.e(e_RB), .l(l_RB), .I(ra_1_oa), .O(rb_1_o), .out_4(rb_1_out_4));
  ALU alu_1 (
    .A(ra_1_ob), .B(rb_1_o), .Code(ri_1_ob), .R(alu_1_r), .x_x_I_O_C_P_S_Z(alu_1_x_x_i_o_c_p_s_z),
    .CS(CS_DEC_ALU), .I___If_result(Comp));
  Hex_Digit_Display hex_digit_display_22 (.value(aff_2_5_out_3));  // open: dp
  Aff_2 aff_2_5 (.in_1(rc_1_out_4), .out_3(aff_2_5_out_3), .out_4(aff_2_5_out_4));  // open: in_2
  Hex_Digit_Display hex_digit_display_23 (.value(aff_2_5_out_4));  // open: dp
  RC rc_1 (.e(e_RC), .l(l_RC), .I(alu_1_r), .O(ra_1_oa), .out_4(rc_1_out_4));
  RE re_1 (.e(e_RE), .l(l_RE), .I(alu_1_x_x_i_o_c_p_s_z), .O(ra_1_oa));
  Hex_Digit_Display hex_digit_display_24 (.value(aff_4_4_out_3));  // open: dp
  Aff_2 aff_2_6 (.in_1(ra_1_oa), .out_3(aff_2_6_out_3), .out_4(aff_2_6_out_4));  // open: in_2
  Hex_Digit_Display hex_digit_display_25 (.value(aff_2_6_out_4));  // open: dp
  Hex_Digit_Display hex_digit_display_26 (.value(aff_2_6_out_3));  // open: dp
  Mem mem_1 (.Bus_A(rad_1_out_6), .Bus_D_O(ra_1_oa), .CS(CSMem), .R_w(R_nw), .Bus_D_I(ra_1_oa));
  Aff_4 aff_4_4 (
    .in_1(rad_1_out_6), .out_3(aff_4_4_out_3), .out_4(aff_4_4_out_4), .out_5(aff_4_4_out_5),
    .out_6(aff_4_4_out_6));  // open: in_2
  Hex_Digit_Display hex_digit_display_27 (.value(aff_4_4_out_4));  // open: dp
  Hex_Digit_Display hex_digit_display_28 (.value(aff_4_4_out_5));  // open: dp
  Hex_Digit_Display hex_digit_display_29 (.value(aff_4_4_out_6));  // open: dp
endmodule

module ALU (
  input  CS,
  input  [3:0] Code,
  input  [7:0] A,
  input  [7:0] B,
  output [7:0] R,
  output [7:0] x_x_I_O_C_P_S_Z,
  output I___If_result
);

  wire adder_1_cout, and_1_out, and_2_out, and_3_out, and_4_out, not_1_out, not_2_out, or_3_out, or_4_out,
       subtractor_1_bout;
  wire [7:0] adder_1_out, divider_1_out, multiplier_1_out, subtractor_1_out;

  Adder adder_1 (.a(A), .b(B), .out(adder_1_out), .cout(adder_1_cout));  // open: cin
  Subtractor subtractor_1 (.a(A), .b(B), .out(subtractor_1_out), .bout(subtractor_1_bout));  // open: bin
  Multiplier multiplier_1 (.a(A), .b(B), .out(multiplier_1_out));  // open: cin, cout
  Divider divider_1 (.a(A), .b(B), .out(divider_1_out), .upper({8{1'b0}}));  // open: rem
  Multiplexer #(.select(4), .width(8)) multiplexer_1 (
    .in2(adder_1_out), .in3(subtractor_1_out), .in4(multiplier_1_out), .in5(divider_1_out),
    .in6(subtractor_1_out), .in7(subtractor_1_out), .in8(subtractor_1_out), .in9(subtractor_1_out),
    .in10(subtractor_1_out), .in11(subtractor_1_out), .out(R), .sel(Code), .en(CS));  // open: in0, in1, in12, in13, in14, in15
  and and_1 (and_1_out, ~B[7], ~A[7], R[7]);  // AND_Gate
  and and_2 (and_2_out, B[7], A[7], ~R[7]);  // AND_Gate
  nor nor_1 (x_x_I_O_C_P_S_Z[0], R[0], R[1], R[2], R[3], R[4], R[5], R[6], R[7]);
  xor xor_1 (x_x_I_O_C_P_S_Z[2], R[0], R[1], R[2], R[3], R[4], R[5], R[6], R[7]);
  or or_1 (x_x_I_O_C_P_S_Z[3], adder_1_cout, subtractor_1_bout);
  or or_2 (x_x_I_O_C_P_S_Z[4], and_1_out, and_2_out);
  not not_1 (not_1_out, x_x_I_O_C_P_S_Z[0]);
  not not_2 (not_2_out, R[7]);
  and and_3 (and_3_out, not_2_out, not_1_out);
  and and_4 (and_4_out, R[7], not_1_out);
  or or_3 (or_3_out, R[7], x_x_I_O_C_P_S_Z[0]);
  or or_4 (or_4_out, not_2_out, x_x_I_O_C_P_S_Z[0]);
  Multiplexer #(.select(4)) multiplexer_2 (
    .in0(1'b0), .in1(1'b0), .in2(1'b0), .in3(1'b0), .in4(1'b0), .in5(1'b0), .in6(x_x_I_O_C_P_S_Z[0]),
    .in7(not_1_out), .in8(and_3_out), .in9(and_4_out), .in10(or_4_out), .in11(or_3_out), .in12(1'b0),
    .in13(1'b0), .in14(1'b0), .in15(1'b0), .out(I___If_result), .sel(Code), .en(CS));

  assign {x_x_I_O_C_P_S_Z[7:5], x_x_I_O_C_P_S_Z[1]} = {2'b00, I___If_result, R[7]};

  // Notes on the sheet:
  //   2 : +
  //   3 : -
  //   4 : *
  //   5 : /
  //   6 : =
  //   7 : !=
  //   8 : >
  //   9 : <
  //   A : >=
  //   B : <=
endmodule

module Mem (
  input  [7:0] Bus_D_I,
  input  [15:0] Bus_A,
  input  CS,
  input  R_w,
  output [7:0] Bus_D_O
);

  wire and_1_out, and_2_out, not_1_out;
  wire [7:0] ram_1_data;

  RAM #(.addrWidth(16), .bus("asynch")) ram_1 (.addr(Bus_A), .data(ram_1_data), .sel(CS), .ld(R_w));  // open: clr
  assign ram_1_data = and_1_out ? Bus_D_I : 8'bz;  // Controlled_Buffer controlled_buffer_1
  and and_1 (and_1_out, CS, not_1_out);
  not not_1 (not_1_out, R_w);
  assign Bus_D_O = and_2_out ? ram_1_data : 8'bz;  // Controlled_Buffer controlled_buffer_2
  and and_2 (and_2_out, CS, R_w);
endmodule

module R16 (
  input  [7:0] I,
  input  ePH,
  input  ePB,
  input  l,
  output [15:0] Contenu,
  output [15:0] O
);

  Register #(.trigger("high")) register_1 (.D(I), .en(ePH), .Q(Contenu[15:8]), .clk(ePH));  // open: clr
  assign O[15:8] = l ? Contenu[15:8] : 8'bz;  // Controlled_Buffer controlled_buffer_1
  Register #(.trigger("high")) register_2 (.D(I), .en(ePB), .Q(Contenu[7:0]), .clk(ePB));  // open: clr
  assign O[7:0] = l ? Contenu[7:0] : 8'bz;  // Controlled_Buffer controlled_buffer_2
endmodule

module RAD (
  input  [7:0] in_1,
  input  in_2,
  input  in_3,
  input  in_4,
  output [15:0] out_5,
  output [15:0] out_6
);

  R16 r16_1 (.ePB(in_2), .ePH(in_3), .l(in_4), .I(in_1), .O(out_6), .Contenu(out_5));
endmodule

module RAP (
  input  [7:0] in_1,
  input  in_2,
  input  in_3,
  input  in_4,
  output [15:0] out_5,
  output [15:0] out_6
);

  R16 r16_1 (.ePB(in_2), .ePH(in_3), .l(in_4), .I(in_1), .O(out_6), .Contenu(out_5));
endmodule

module PC (
  input  [15:0] I,
  input  e,
  input  INC,
  input  l,
  input  RAZ,
  input  Clock,
  output [15:0] out_7,
  output [15:0] O
);

  Counter #(.width(16), .max('hffff)) counter_1 (
    .load(e), .D(I), .count(INC), .Q(out_7), .clk(Clock), .clr(RAZ));  // open: carry
  assign O = l ? out_7 : 16'bz;  // Controlled_Buffer controlled_buffer_1
endmodule

module R8 (
  input  [7:0] I,
  input  e,
  input  l,
  output [7:0] O
);

  wire [7:0] register_1_q;

  Register #(.trigger("high")) register_1 (.D(I), .en(e), .Q(register_1_q), .clk(e));  // open: clr
  assign O = l ? register_1_q : 8'bz;  // Controlled_Buffer controlled_buffer_1
endmodule

module RA (
  input  [7:0] I,
  input  lA,
  input  e,
  input  lB,
  output [7:0] out_5,
  output [7:0] oA,
  output [7:0] oB
);

  Register #(.trigger("high")) register_1 (.D(I), .en(e), .Q(out_5), .clk(e));  // open: clr
  assign oA = lA ? out_5 : 8'bz;  // Controlled_Buffer controlled_buffer_1
  assign oB = lB ? out_5 : 8'bz;  // Controlled_Buffer controlled_buffer_2
endmodule

module RB (
  input  [7:0] I,
  input  e,
  input  l,
  output [7:0] out_4,
  output [7:0] O
);

  Register #(.trigger("high")) register_1 (.D(I), .en(e), .Q(out_4), .clk(e));  // open: clr
  assign O = l ? out_4 : 8'bz;  // Controlled_Buffer controlled_buffer_1
endmodule

module RC (
  input  [7:0] I,
  input  e,
  input  l,
  output [7:0] out_4,
  output [7:0] O
);

  Register #(.trigger("high")) register_1 (.D(I), .en(e), .Q(out_4), .clk(e));  // open: clr
  assign O = l ? out_4 : 8'bz;  // Controlled_Buffer controlled_buffer_1
endmodule

module RE (
  input  [7:0] I,
  input  e,
  input  l,
  output [7:0] O
);

  wire [7:0] register_1_q;

  Register #(.trigger("high")) register_1 (.D(I), .en(e), .Q(register_1_q), .clk(e));  // open: clr
  assign O = l ? register_1_q : 8'bz;  // Controlled_Buffer controlled_buffer_1
endmodule

module RI (
  input  [7:0] I,
  input  eRI,
  input  lRIh,
  input  lRIb,
  output [7:0] out_5,
  output [3:0] oH,
  output [3:0] oB
);

  Register #(.width(4), .trigger("high")) register_1 (.D(I[7:4]), .en(eRI), .Q(out_5[7:4]), .clk(eRI));  // open: clr
  assign oH = lRIh ? out_5[7:4] : 4'bz;  // Controlled_Buffer controlled_buffer_1
  Register #(.width(4), .trigger("high")) register_2 (.D(I[3:0]), .en(eRI), .Q(out_5[3:0]), .clk(eRI));  // open: clr
  assign oB = lRIb ? out_5[3:0] : 4'bz;  // Controlled_Buffer controlled_buffer_2
endmodule

module UCom (
  input  [3:0] in_1,
  input  in_2,
  input  in_3,
  input  in_4,
  output [7:0] out_5,
  output [23:0] out_6,
  output [7:0] out_7,
  output CS_DEC_ALU
);

  wire or_1_out;
  wire [7:0] drom_1_out_3, muxdecode_1_out_3;

  MuxDecode muxdecode_1 (.in_1(in_1), .out_3(muxdecode_1_out_3), .in_2(out_7[4]));
  MuxEtat muxetat_1 (.in_1(in_2), .out_3(muxdecode_1_out_3), .in_2(out_7[3]));
  or or_1 (or_1_out, in_4, out_7[5]);
  CompteurRom compteurrom_1 (
    .e(out_7[7]), .INC(out_7[6]), .RAZ(or_1_out), .in_1(muxdecode_1_out_3), .l(1'b1), .out_7(out_5), .h(in_3));
  DRom drom_1 (.in_2(out_5), .out_3(drom_1_out_3), .in_1(in_3));
  Rom rom_1 (.in_1(drom_1_out_3), .out_3(out_6), .out_4({out_7[7:3], CS_DEC_ALU, out_7[1:0]}), .in_2(1'b1));

  assign out_7[2] = CS_DEC_ALU;
endmodule

module Rom (
  input  [7:0] in_1,
  input  in_2,
  output [23:0] out_3,
  output [7:0] out_4
);

  ROM #(.dataWidth(32)) rom_1 (.addr(in_1), .data({out_3, out_4}), .sel(in_2));

  // Notes on the sheet:
  //   contents of rom_1 (hex, n*v repeats v):
  //   c00a0040 40890 8*0 840 820 4*0 c0020140 840 c0020240 840 c0420040 80200c20 10*0 c0020140 840
  //   c0020240 c0400c40 c0020140 840 c0020240 80200c20 0 0 0 c0020140 840 c0020240 c0400c40 c1020040
  //   a900844 c0020140 840 c0020240 84000c20 6*0 c0020140 840 c0020240 c0400c40 c0020140 840 c0020240
  //   c1000c40 a900044 c0020140 840 c0020240 84000c20 0 0 0 c0022040 840 c0024040 18020 12*0 c0020140 840
  //   c0020240 c0400c40 c1020040 2290088c 10*0 c0020140 840 c0020240 c0400c40 c0020140 840 c0020240
  //   c1000440 2290088c
endmodule

module CompteurRom (
  input  [7:0] in_1,
  input  h,
  input  l,
  input  e,
  input  INC,
  input  RAZ,
  output [7:0] out_7
);

  wire [7:0] counter_1_q;

  Counter counter_1 (.load(e), .D(in_1), .count(INC), .Q(counter_1_q), .clk(h), .clr(RAZ));  // open: carry
  assign out_7 = l ? counter_1_q : 8'bz;  // Controlled_Buffer controlled_buffer_1
endmodule

module DRom (
  input  in_1,
  input  [7:0] in_2,
  output [7:0] out_3
);

  D_Flip_Flop #(.trigger("falling")) d_ff_1 (.clk(in_1), .D(in_2[0]), .Q(out_3[0]));  // open: Qn, preset, en, reset
  D_Flip_Flop #(.trigger("falling")) d_ff_2 (.clk(in_1), .D(in_2[1]), .Q(out_3[1]));  // open: Qn, preset, en, reset
  D_Flip_Flop #(.trigger("falling")) d_ff_3 (.clk(in_1), .D(in_2[2]), .Q(out_3[2]));  // open: Qn, preset, en, reset
  D_Flip_Flop #(.trigger("falling")) d_ff_4 (.clk(in_1), .D(in_2[3]), .Q(out_3[3]));  // open: Qn, preset, en, reset
  D_Flip_Flop #(.trigger("falling")) d_ff_5 (.clk(in_1), .D(in_2[4]), .Q(out_3[4]));  // open: Qn, preset, en, reset
  D_Flip_Flop #(.trigger("falling")) d_ff_6 (.clk(in_1), .D(in_2[5]), .Q(out_3[5]));  // open: Qn, preset, en, reset
  D_Flip_Flop #(.trigger("falling")) d_ff_7 (.clk(in_1), .D(in_2[6]), .Q(out_3[6]));  // open: Qn, preset, en, reset
  D_Flip_Flop #(.trigger("falling")) d_ff_8 (.clk(in_1), .D(in_2[7]), .Q(out_3[7]));  // open: Qn, preset, en, reset
endmodule

module MuxDecode (
  input  [3:0] in_1,
  input  in_2,
  output [7:0] out_3
);

  Multiplexer #(.select(4), .width(8)) multiplexer_1 (
    .in0({8{1'b0}}), .in1(8'h10), .in2(8'h20), .in3(8'h30), .in4(8'h40), .in5(8'h50), .in6(8'h60),
    .in7(8'h70), .out(out_3), .sel(in_1), .en(in_2));  // open: in8, in9, in10, in11, in12, in13, in14, in15
endmodule

module MuxEtat (
  input  in_1,
  input  in_2,
  output [7:0] out_3
);

  Multiplexer #(.width(8)) multiplexer_1 (.in0({8{1'b0}}), .in1(8'ha), .out(out_3), .sel(in_1), .en(in_2));
endmodule

module Aff_4 (
  input  [15:0] in_1,
  input  [15:0] in_2,
  output [3:0] out_3,
  output [3:0] out_4,
  output [3:0] out_5,
  output [3:0] out_6
);


  assign in_2 = in_1;
  assign out_3 = in_1[15:12];
  assign out_4 = in_1[11:8];
  assign out_5 = in_1[7:4];
  assign out_6 = in_1[3:0];
endmodule

module Aff_2 (
  input  [7:0] in_1,
  input  [7:0] in_2,
  output [3:0] out_3,
  output [3:0] out_4
);


  assign in_2 = in_1;
  assign out_3 = in_1[7:4];
  assign out_4 = in_1[3:0];
endmodule
